# Fritzing sketch Lichtuhr (saved by Fritzing 0.9.2b)

parts:
  Bauteil1 = Arduino Uno (Rev3)
  R1 = Slide Potentiometer [maximum_resistance=100kΩ]
  LED1 = LEDs [package=led10mm]
  LED2 = LEDs [package=led10mm]
  LED3 = LEDs [package=led10mm]
  LED4 = LEDs [package=led10mm]
  LED5 = LEDs [package=led10mm]
  LED6 = LEDs [package=led10mm]
  LED7 = LEDs [package=led10mm]
  LED8 = LEDs [package=led10mm]
  Bauteil2 = Real Time Clock Module - DS1307 RTC Breakout Board
  R2 = Resistor [tolerance=±5% resistance=220 package="0805 [SMD]"]
  R3 = Resistor [tolerance=±5% resistance=220 package="0805 [SMD]"]
  M1 = DC Motor  # not connected

nets:
  N1: Bauteil1.A0, R1.wiper
  N2: Bauteil1.A4/SDA, Bauteil2.SDA
  N3: Bauteil1.A5/SCL, Bauteil2.SCL
  N4: Bauteil1.D8, LED1.C
  N5: Bauteil1.D9_PWM, LED3.C
  N6: Bauteil1.D2, LED5.C
  N7: Bauteil1.D3_PWM, LED4.C
  N8: Bauteil1.D4, LED7.C
  N9: Bauteil1.D5_PWM, LED6.C
  N10: Bauteil1.D6_PWM, LED8.C
  N11: Bauteil1.D7, LED2.C
  N12: Bauteil1.5V, R1.leg1, R3.Pin_1
  N13: Bauteil1.GND, R1.leg2
  N14: LED3.A, R2.Pin_0

notes:
  GND
  Motor-B VCC
  Motor-B B-IB
  Motor-A B-IA
  Motor-A A-IB
  A-IA
  L9110 H-Bridge
